# Fritzing sketch WiringDiagram (saved by Fritzing 0.9.3b)
breadboards: 2

parts:
  PWM1 = PCA9685 16x12-bit PWM Breakout
  S1 = Pushbutton [package="[THT]"]
  S2 = Pushbutton [package="[THT]"]
  S3 = Pushbutton [package="[THT]"]
  S4 = Pushbutton [package="[THT]"]
  S5 = Pushbutton [package="[THT]"]
  S6 = Pushbutton [package="[THT]"]
  S7 = Pushbutton [package="[THT]"]
  S8 = Pushbutton [package="[THT]"]
  S9 = Pushbutton [package="[THT]"]
  S10 = Pushbutton [package="[THT]"]
  S11 = Pushbutton [package="[THT]"]
  S12 = Pushbutton [package="[THT]"]
  S13 = Pushbutton [package="[THT]"]
  S14 = Pushbutton [package="[THT]"]
  S15 = Pushbutton [package="[THT]"]
  LED1 = smd LED [color="Red (633nm)" package="0805 [SMD]"]
  LED2 = smd LED [color="Red (633nm)" package="0805 [SMD]"]
  LED3 = smd LED [color="Red (633nm)" package="0805 [SMD]"]  # not connected
  LED4 = smd LED [color="Red (633nm)" package="0805 [SMD]"]  # not connected
  LED5 = smd LED [color="Red (633nm)" package="0805 [SMD]"]  # not connected
  LED6 = smd LED [color="Red (633nm)" package="0805 [SMD]"]  # not connected
  LED7 = smd LED [color="Red (633nm)" package="0805 [SMD]"]  # not connected
  LED8 = smd LED [color="Red (633nm)" package="0805 [SMD]"]  # not connected
  LED9 = smd LED [color="Red (633nm)" package="0805 [SMD]"]  # not connected
  LED10 = smd LED [color="Red (633nm)" package="0805 [SMD]"]  # not connected
  LED11 = smd LED [color="Red (633nm)" package="0805 [SMD]"]  # not connected
  LED12 = smd LED [color="Red (633nm)" package="0805 [SMD]"]  # not connected
  LED13 = smd LED [color="Red (633nm)" package="0805 [SMD]"]  # not connected
  LED14 = smd LED [color="Red (633nm)" package="0805 [SMD]"]  # not connected
  LED15 = smd LED [color="Red (633nm)" package="0805 [SMD]"]  # not connected
  5v_Power_Supply = Power plug
  Raspberry_Pi1 = Raspberry Pi B+
  J1 = Camdenboss CTB0158-11 [part_number=CTB0158-11 package=THT]
  J2 = Camdenboss CTB0158-11 [part_number=CTB0158-11 package=THT]
  U1 = USB_AB [package=usb-ab-micro-smd]  # not connected
  U2 = USB_AB [package=usb-ab-micro-smd]  # not connected
  U3 = USB_AB [package=usb-ab-micro-smd]  # not connected
  U4 = USB_AB [package=usb-ab-micro-smd]  # not connected
  U5 = USB_AB [package=usb-ab-micro-smd]  # not connected
  U6 = USB_AB [package=usb-ab-micro-smd]  # not connected
  U7 = USB_AB [package=usb-ab-micro-smd]  # not connected
  U8 = USB_AB [package=usb-ab-micro-smd]  # not connected
  To_Raspberry_Pi_Micro_USB = USB_AB [package=usb-ab-micro-smd]
  Relay_Module_Power_Plug = USB_AB [package=usb-ab-micro-smd]

nets:
  N1: PWM1.no_name_yet#14, LED2.anode
  N2: PWM1.no_name_yet#15, LED1.anode
  N3: PWM1.no_name_yet#503, Raspberry_Pi1.GPIO3
  N4: PWM1.no_name_yet#504, Raspberry_Pi1.GPIO2
  N5: PWM1.no_name_yet#701, PWM1.no_name_yet#1014, PWM1.no_name_yet#1015, LED1.cathode, LED2.cathode, J2.terminal_1
  N6: PWM1.no_name_yet#706, J1.terminal_1
  N7: S1.Pin_1, S1.Pin_2, S2.Pin_1, S2.Pin_2, S3.Pin_1, S3.Pin_2, S4.Pin_1, S4.Pin_2, S5.Pin_1, S5.Pin_2, S6.Pin_1, S6.Pin_2, S7.Pin_1, S7.Pin_2, S8.Pin_1, S8.Pin_2, S9.Pin_1, S9.Pin_2, S10.Pin_1, S10.Pin_2, S11.Pin_1, S11.Pin_2, S12.Pin_1, S12.Pin_2, S13.Pin_1, S13.Pin_2, S14.Pin_1, S14.Pin_2, S15.Pin_1, S15.Pin_2, Raspberry_Pi1.GND
  N8: S1.Pin_3, S1.Pin_4, Raspberry_Pi1.GPIO5
  N9: S2.Pin_3, S2.Pin_4, Raspberry_Pi1.GPIO6
  N10: S3.Pin_3, S3.Pin_4, Raspberry_Pi1.GPIO7
  N11: S4.Pin_3, S4.Pin_4, Raspberry_Pi1.GPIO8
  N12: S5.Pin_3, S5.Pin_4, Raspberry_Pi1.GPIO10
  N13: S6.Pin_3, S6.Pin_4, Raspberry_Pi1.GPIO9
  N14: S7.Pin_3, S7.Pin_4, Raspberry_Pi1.GPIO11
  N15: S8.Pin_3, S8.Pin_4, Raspberry_Pi1.GPIO12
  N16: S9.Pin_3, S9.Pin_4, Raspberry_Pi1.GPIO13
  N17: S10.Pin_3, S10.Pin_4, Raspberry_Pi1.GPIO14
  N18: S11.Pin_3, S11.Pin_4, Raspberry_Pi1.GPIO15
  N19: S12.Pin_3, S12.Pin_4, Raspberry_Pi1.GPIO16
  N20: S13.Pin_3, S13.Pin_4, Raspberry_Pi1.GPIO17
  N21: S14.Pin_3, S14.Pin_4, Raspberry_Pi1.GPIO4
  N22: S15.Pin_3, S15.Pin_4, Raspberry_Pi1.GPIO18
  N23: 5v_Power_Supply.GND, J2.terminal_11
  N24: 5v_Power_Supply.VCC, J1.terminal_11
  N25: J1.terminal_2, To_Raspberry_Pi_Micro_USB.VBUS
  N26: J1.terminal_3, Relay_Module_Power_Plug.VBUS
  N27: J2.terminal_2, To_Raspberry_Pi_Micro_USB.D-
  N28: J2.terminal_3, Relay_Module_Power_Plug.D-
